// Logisim project X64000.circ as structural Verilog: 7 circuits, main circuit RST
module RST (
  input  ResetIssue,
  output [15:0] ResetLine
);

  and and_1 (ResetLine[15], ResetIssue, 1'b1);

  assign ResetLine[14:0] = {15{ResetLine[15]}};

  // Other names for the same wires on the sheet: RST[15:0] = {16{ResetLine[15]}}

  // Notes on the sheet:
  //   32k reset line
endmodule

module RU (
  input  [63:0] RegisterValue,
  input  [2:0] RegisterIndex,
  input  RegAccept,
  output [2:0] RegisterIndexValue,
  output [63:0] RegisterOutputValue
);

  wire Clk_out, RegWrite, undriven, undriven_2;

  and and_1 (RegWrite, 1'b1, RegAccept);
  Register #(.width(64)) register_1 (
    .D(RegisterValue), .en(RegWrite), .clk(Clk_out), .Q(RegisterOutputValue), .clr(undriven));
  // NoConnect on undriven
  Clock Clk (.out(Clk_out));
  Register #(.width(3)) IndexRegister (
    .D(RegisterIndex), .en(RegWrite), .clk(Clk_out), .Q(RegisterIndexValue), .clr(undriven_2));
  // NoConnect on undriven_2

  // Other names for the same wires on the sheet: RegisterValueTunnel[63:0] = RegisterValue

  // Notes on the sheet:
  //   32k register file
  //   we get the index and put inside
  //   this register
  //   This is like an array
endmodule

module X64 (
  input  [63:0] AssignValue,
  input  [2:0] RegisterId,
  input  [2:0] InputRegisterId,
  output [63:0] out_4
);

  wire Accept, not_1_out, or_1_out, pull_resistor_1_node, x1002_2_drain, x1002_3_drain, xor_1_out;

  Pull_Resistor pull_resistor_1 (.node(pull_resistor_1_node));
  X1002 x1002_1 (.LA(RegisterId[1]), .LB(InputRegisterId[1]), .SRC(InputRegisterId[1]), .DRAIN(Accept));
  X1002 x1002_2 (.LA(RegisterId[0]), .LB(InputRegisterId[0]), .SRC(InputRegisterId[0]), .DRAIN(x1002_2_drain));
  X1002 x1002_3 (.LA(InputRegisterId[2]), .LB(RegisterId[2]), .SRC(RegisterId[2]), .DRAIN(x1002_3_drain));
  RU RegUni (
    .RegisterValue(AssignValue), .RegisterIndex(RegisterId), .RegAccept(pull_resistor_1_node),
    .RegisterOutputValue(out_4));  // open: RegisterIndexValue
  not not_1 (not_1_out, or_1_out);
  or or_1 (or_1_out, x1002_2_drain, x1002_3_drain);
  not not_2 (pull_resistor_1_node, xor_1_out);
  xor xor_1 (xor_1_out, Accept, not_1_out);
endmodule

module X1001 (
  input  G,
  input  S,
  output O
);

  wire not_1_out;

  Pull_Resistor pull_resistor_1 (.node(O));
  not not_1 (not_1_out, G);
  Transistor transistor_1 (.in(S), .out(O), .gate(not_1_out));
endmodule

module X1002 (
  input  LA,
  input  LB,
  input  SRC,
  output DRAIN
);

  wire not_1_out, not_2_out, pull_resistor_1_node;

  not not_1 (not_1_out, LA);
  Pull_Resistor pull_resistor_1 (.node(pull_resistor_1_node));
  not not_2 (not_2_out, LB);
  Pull_Resistor pull_resistor_2 (.node(DRAIN));
  Transistor transistor_1 (.in(pull_resistor_1_node), .out(DRAIN), .gate(not_1_out));
  Transistor transistor_2 (.in(SRC), .out(pull_resistor_1_node), .gate(not_2_out));
endmodule

module X1003 (
  input  in_1,
  input  in_2,
  input  in_3,
  input  in_4,
  output out_5,
  output out_6
);

  Pull_Resistor pull_resistor_1 (.node(out_5));
  Pull_Resistor pull_resistor_2 (.node(out_5));
  Transistor transistor_1 (.in(in_3), .out(out_5), .gate(in_1));
  Transistor transistor_2 (.in(in_3), .out(out_5), .gate(in_1));

  assign in_2 = in_1;
  assign in_4 = in_3;
  assign out_6 = out_5;
endmodule

module X1004 (
  input  in_1,
  input  in_2,
  input  in_3,
  input  in_4,
  output out_5
);

  wire not_1_out, not_2_out, not_3_out, pull_resistor_2_node, pull_resistor_3_node;

  Pull_Resistor pull_resistor_1 (.node(out_5));
  not not_1 (not_1_out, in_1);
  Pull_Resistor pull_resistor_2 (.node(pull_resistor_2_node));
  not not_2 (not_2_out, in_2);
  Pull_Resistor pull_resistor_3 (.node(pull_resistor_3_node));
  not not_3 (not_3_out, in_3);
  Transistor transistor_1 (.in(pull_resistor_2_node), .out(out_5), .gate(not_1_out));
  Transistor transistor_2 (.in(pull_resistor_3_node), .out(pull_resistor_2_node), .gate(not_2_out));
  Transistor transistor_3 (.in(in_4), .out(pull_resistor_3_node), .gate(not_3_out));
endmodule
